// Logisim project alu.circ as structural Verilog: 1 circuit, main circuit arithmetic_logic_unit
module arithmetic_logic_unit (
  input  [7:0] A,
  input  [7:0] B,
  input  [2:0] in_3,
  output SIGN,
  output [7:0] Q,
  output Carry
);

  wire adder_1_cout, not_1_out;
  wire [7:0] adder_1_out, and_1_out, controlled_buffer_1_out, controlled_inverter_1_out, or_1_out,
       shifter_1_out, shifter_2_out, subtractor_1_out, xor_1_out;

  Shifter shifter_1 (.in(A), .\dist (3'b001), .out(shifter_1_out));
  Shifter #(.shift("lr")) shifter_2 (.in(A), .\dist (3'b001), .out(shifter_2_out));
  Adder adder_1 (.a(A), .b(B), .out(adder_1_out), .cout(adder_1_cout));  // open: cin
  Subtractor subtractor_1 (.a(A), .b(B), .out(subtractor_1_out), .bout(SIGN));  // open: bin
  assign and_1_out = A & B;  // AND_Gate and_1, 8 bits wide
  assign or_1_out = A | B;  // OR_Gate or_1, 8 bits wide
  assign xor_1_out = A ^ B;  // XOR_Gate xor_1, 8 bits wide
  assign controlled_inverter_1_out = SIGN ? ~subtractor_1_out : 8'bz;  // Controlled_Inverter controlled_inverter_1
  not not_1 (not_1_out, SIGN);
  assign controlled_buffer_1_out = not_1_out ? subtractor_1_out : 8'bz;  // Controlled_Buffer controlled_buffer_1
  Adder adder_2 (.a(8'h1), .b(controlled_inverter_1_out), .out(controlled_buffer_1_out));  // open: cin, cout
  Multiplexer #(.select(3), .width(8)) multiplexer_1 (
    .in0({8{1'b0}}), .in1(adder_1_out), .in2(controlled_buffer_1_out), .in3(and_1_out), .in4(or_1_out),
    .in5(xor_1_out), .in6(shifter_1_out), .in7(shifter_2_out), .out(Q), .sel(in_3));
  Multiplexer #(.select(3)) multiplexer_2 (
    .in0(1'b0), .in1(adder_1_cout), .in2(1'b0), .in3(1'b0), .in4(1'b0), .in5(1'b0), .in6(A[0]), .in7(A[7]),
    .out(Carry), .sel(in_3));
endmodule
