// Logisim project sap2_main.circ as structural Verilog: 1 circuit, main circuit main
module main (
  input  in_1,
  input  in_2,
  input  in_3,
  input  in_4,
  input  in_5,
  input  [3:0] in_6,
  input  in_7,
  input  in_8,
  input  in_9,
  input  in_10,
  input  in_11,
  input  in_12,
  input  in_13,
  input  in_14,
  input  in_15,
  input  in_16,
  input  in_17,
  input  in_18,
  input  in_19,
  input  in_20,
  input  in_21,
  input  in_22,
  input  in_23,
  input  in_24,
  input  in_25,
  input  in_26,
  input  in_27,
  input  in_28,
  input  in_29,
  output [15:0] out_30,
  output [15:0] out_31,
  output [15:0] out_32,
  output [3:0] out_33,
  output [2:0] out_34,
  output [7:0] out_35,
  output [15:0] out_36
);

  wire arithmetic_logic_unit_1_carry, arithmetic_logic_unit_1_sign, CLK, nor_1_out;
  wire [7:0] ram_1_dout, register_8_1_q1, register_8_2_o1, register_8_3_o1;
  wire [15:0] register_16_1_q1;

  Clock clock_1 (.out(CLK));
  RAM #(.addrWidth(16), .asyncread("true")) ram_1 (
    .addr(register_16_1_q1), .we(in_12), .oe(in_13), .clk(CLK), .din(out_30[7:0]), .dout(ram_1_dout));
  pc pc_1 (.EN(in_3), .LOAD(in_4), .COUNT(in_5), .CLK(CLK), .D_in(out_30), .Q_out(out_30), .O_out(out_31));
  register_16 register_16_1 (
    .D1(out_30[0]), .D2(out_30[1]), .D3(out_30[2]), .D4(out_30[3]), .D5(out_30[4]), .D6(out_30[5]),
    .D7(out_30[6]), .D8(out_30[7]), .D9(out_30[8]), .D10(out_30[9]), .D11(out_30[10]), .D12(out_30[11]),
    .D13(out_30[12]), .D14(out_30[13]), .D15(out_30[14]), .D16(out_30[15]), .LOAD(in_8), .CLK(CLK),
    .EN(in_9), .O1(out_32[0]), .O2(out_32[1]), .O3(out_32[2]), .O4(out_32[3]), .O5(out_32[4]),
    .O6(out_32[5]), .O7(out_32[6]), .O8(out_32[7]), .O9(out_32[8]), .O10(out_32[9]), .O11(out_32[10]),
    .O12(out_32[11]), .O13(out_32[12]), .O14(out_32[13]), .O15(out_32[14]), .O16(out_32[15]),
    .Q1(register_16_1_q1[0]), .Q2(register_16_1_q1[1]), .Q3(register_16_1_q1[2]), .Q4(register_16_1_q1[3]),
    .Q5(register_16_1_q1[4]), .Q6(register_16_1_q1[5]), .Q7(register_16_1_q1[6]), .Q8(register_16_1_q1[7]),
    .Q9(register_16_1_q1[8]), .Q10(register_16_1_q1[9]), .Q11(register_16_1_q1[10]),
    .Q12(register_16_1_q1[11]), .Q13(register_16_1_q1[12]), .Q14(register_16_1_q1[13]),
    .Q15(register_16_1_q1[14]), .Q16(register_16_1_q1[15]));
  register_8 register_8_1 (
    .D1(ram_1_dout[0]), .D2(ram_1_dout[1]), .D3(ram_1_dout[2]), .D4(ram_1_dout[3]), .D5(ram_1_dout[4]),
    .D6(ram_1_dout[5]), .D7(ram_1_dout[6]), .D8(ram_1_dout[7]), .LOAD(in_14), .CLK(CLK), .EN(in_15),
    .Q1(register_8_1_q1[0]), .Q2(register_8_1_q1[1]), .Q3(register_8_1_q1[2]), .Q4(register_8_1_q1[3]),
    .Q5(register_8_1_q1[4]), .Q6(register_8_1_q1[5]), .Q7(register_8_1_q1[6]), .Q8(register_8_1_q1[7]));  // open: O1, O2, O3, O4, O5, O6, O7, O8
  Demultiplexer #(.tristate("true"), .width(8)) demultiplexer_1 (
    .out0(out_30[7:0]), .out1(out_30[15:8]), .in(register_8_1_q1), .sel(in_16));
  register_z16bits register_z16bits_1 (
    .D1(out_30[0]), .D2(out_30[1]), .D3(out_30[2]), .D4(out_30[3]), .D5(out_30[4]), .D6(out_30[5]),
    .D7(out_30[6]), .D8(out_30[7]), .D9(out_30[8]), .D10(out_30[9]), .D11(out_30[10]), .D12(out_30[11]),
    .D13(out_30[12]), .D14(out_30[13]), .D15(out_30[14]), .D16(out_30[15]), .CLK(CLK), .LOAD1(in_19),
    .LOAD2(in_20), .EN1(in_21), .EN2(in_22), .Q1(out_30[0]), .Q2(out_30[1]), .Q3(out_30[2]), .Q4(out_30[3]),
    .Q5(out_30[4]), .Q6(out_30[5]), .Q7(out_30[6]), .Q8(out_30[7]), .Q9(out_30[8]), .Q10(out_30[9]),
    .Q11(out_30[10]), .Q12(out_30[11]), .Q13(out_30[12]), .Q14(out_30[13]), .Q15(out_30[14]), .Q16(out_30[15]));  // open: O1, O2, O3, O4, O5, O6, O7, O8, O9, O10, O11, O12, O13, O14, O15, O16
  register_16 register_16_2 (
    .D1(out_30[0]), .D2(out_30[1]), .D3(out_30[2]), .D4(out_30[3]), .D5(out_30[4]), .D6(out_30[5]),
    .D7(out_30[6]), .D8(out_30[7]), .D9(out_30[8]), .D10(out_30[9]), .D11(out_30[10]), .D12(out_30[11]),
    .D13(out_30[12]), .D14(out_30[13]), .D15(out_30[14]), .D16(out_30[15]), .LOAD(in_27), .CLK(CLK),
    .EN(in_29), .Q1(out_30[0]), .Q2(out_30[1]), .Q3(out_30[2]), .Q4(out_30[3]), .Q5(out_30[4]),
    .Q6(out_30[5]), .Q7(out_30[6]), .Q8(out_30[7]), .Q9(out_30[8]), .Q10(out_30[9]), .Q11(out_30[10]),
    .Q12(out_30[11]), .Q13(out_30[12]), .Q14(out_30[13]), .Q15(out_30[14]), .Q16(out_30[15]));  // open: O1, O2, O3, O4, O5, O6, O7, O8, O9, O10, O11, O12, O13, O14, O15, O16
  register_8 register_8_2 (
    .D1(out_30[0]), .D2(out_30[1]), .D3(out_30[2]), .D4(out_30[3]), .D5(out_30[4]), .D6(out_30[5]),
    .D7(out_30[6]), .D8(out_30[7]), .LOAD(in_1), .CLK(CLK), .EN(in_2), .O1(register_8_2_o1[0]),
    .O2(register_8_2_o1[1]), .O3(register_8_2_o1[2]), .O4(register_8_2_o1[3]), .O5(register_8_2_o1[4]),
    .O6(register_8_2_o1[5]), .O7(register_8_2_o1[6]), .O8(register_8_2_o1[7]), .Q1(out_30[0]),
    .Q2(out_30[1]), .Q3(out_30[2]), .Q4(out_30[3]), .Q5(out_30[4]), .Q6(out_30[5]), .Q7(out_30[6]),
    .Q8(out_30[7]));
  register_8 register_8_3 (
    .D1(out_30[0]), .D2(out_30[1]), .D3(out_30[2]), .D4(out_30[3]), .D5(out_30[4]), .D6(out_30[5]),
    .D7(out_30[6]), .D8(out_30[7]), .LOAD(in_10), .CLK(CLK), .EN(in_11), .O1(register_8_3_o1[0]),
    .O2(register_8_3_o1[1]), .O3(register_8_3_o1[2]), .O4(register_8_3_o1[3]), .O5(register_8_3_o1[4]),
    .O6(register_8_3_o1[5]), .O7(register_8_3_o1[6]), .O8(register_8_3_o1[7]), .Q1(out_30[0]),
    .Q2(out_30[1]), .Q3(out_30[2]), .Q4(out_30[3]), .Q5(out_30[4]), .Q6(out_30[5]), .Q7(out_30[6]),
    .Q8(out_30[7]));
  register_8 register_8_4 (
    .D1(out_30[0]), .D2(out_30[1]), .D3(out_30[2]), .D4(out_30[3]), .D5(out_30[4]), .D6(out_30[5]),
    .D7(out_30[6]), .D8(out_30[7]), .LOAD(in_17), .CLK(CLK), .EN(in_18), .Q1(out_30[0]), .Q2(out_30[1]),
    .Q3(out_30[2]), .Q4(out_30[3]), .Q5(out_30[4]), .Q6(out_30[5]), .Q7(out_30[6]), .Q8(out_30[7]));  // open: O1, O2, O3, O4, O5, O6, O7, O8
  register_8 register_8_5 (
    .D1(out_30[0]), .D2(out_30[1]), .D3(out_30[2]), .D4(out_30[3]), .D5(out_30[4]), .D6(out_30[5]),
    .D7(out_30[6]), .D8(out_30[7]), .LOAD(in_23), .CLK(CLK), .EN(in_24), .Q1(out_30[0]), .Q2(out_30[1]),
    .Q3(out_30[2]), .Q4(out_30[3]), .Q5(out_30[4]), .Q6(out_30[5]), .Q7(out_30[6]), .Q8(out_30[7]));  // open: O1, O2, O3, O4, O5, O6, O7, O8
  register_8 register_8_6 (
    .D1(out_30[0]), .D2(out_30[1]), .D3(out_30[2]), .D4(out_30[3]), .D5(out_30[4]), .D6(out_30[5]),
    .D7(out_30[6]), .D8(out_30[7]), .LOAD(in_26), .CLK(CLK), .EN(in_28), .O1(out_35[0]), .O2(out_35[1]),
    .O3(out_35[2]), .O4(out_35[3]), .O5(out_35[4]), .O6(out_35[5]), .O7(out_35[6]), .O8(out_35[7]),
    .Q1(out_30[0]), .Q2(out_30[1]), .Q3(out_30[2]), .Q4(out_30[3]), .Q5(out_30[4]), .Q6(out_30[5]),
    .Q7(out_30[6]), .Q8(out_30[7]));
  ring ring_1 (.CLR(in_25), .CLK(CLK), .STATE(out_33));
  arithmetic_logic_unit arithmetic_logic_unit_1 (
    .A(register_8_2_o1), .B(register_8_3_o1), .OP(in_6), .SIGN(arithmetic_logic_unit_1_sign),
    .Q(out_30[7:0]), .Carry(arithmetic_logic_unit_1_carry));
  nor nor_1 (nor_1_out, out_30[0], out_30[1], out_30[2], out_30[3], out_30[4], out_30[5], out_30[6], out_30[7]);
  ROM #(.addrWidth(16), .dataWidth(32)) rom_1 (.addr({1'b0, out_34, out_33, out_35}));  // open: data
  flags flags_1 (
    .Carry(arithmetic_logic_unit_1_carry), .Sign(arithmetic_logic_unit_1_sign), .Zero(nor_1_out),
    .LOAD(in_7), .CLK(CLK), .Carry_out(out_34[0]), .Sign_out(out_34[1]), .Zero_out(out_34[2]));

  assign out_36 = {1'b0, out_34, out_33, out_35};

  // Other names for the same wires on the sheet: FLAG[2:0] = out_34

  // Notes on the sheet:
  //   Random Access Memory
  //   L Register
  //   Program Counter
  //   Memory Address Register
  //   Memory Data Register
  //    Z Register
  //   Accumulator Register
  //   Temporary Register
  //   Register B
  //   Register C
  //   Instruction Register
  //   contents of rom_1 (hex, n*v repeats v):
  //   8*9 8*0 8*d4 8*0 8*10000100 216*0 8*9 8*0 8*d4 8*0 8*10000100 216*0 8*9 8*0 8*d4 8*0 8*10000100
  //   216*0 8*9 8*0 8*d4 8*0 8*10000100 216*0 8*9 8*0 8*d4 8*0 8*10000100 216*0 8*9 8*0 8*d4 8*0
  //   8*10000100 216*0 8*9 8*0 8*d4 8*0 8*10000100 216*0 8*9 8*0 8*d4 8*0 8*10000100 216*0 8*9 8*0 8*d4
  //   8*0 8*10000100 216*0 8*9 8*0 8*d4 8*0 8*10000100 216*0 8*9 8*0 8*d4 8*0 8*10000100 216*0 8*9 8*0
  //   8*d4 8*0 8*10000100 216*0 8*9 8*0 8*d4 8*0 8*10000100 216*0 8*9 8*0 8*d4 8*0 8*10000100 216*0 8*9
  //   8*0 8*d4 8*0 8*10000100 216*0 8*9 8*0 8*d4 8*0 8*10000100 216*0 8*9 8*0 8*d4 8*0 8*10000100 216*0
  //   8*9 8*0 8*d4 8*0 8*10000100 216*0 8*9 8*0 8*d4 8*0 8*10000100 216*0 8*9 8*0 8*d4 8*0 8*10000100
  //   216*0 8*9 8*0 8*d4 8*0 8*10000100 216*0 8*9 8*0 8*d4 8*0 8*10000100 216*0 8*9 8*0 8*d4 8*0
  //   8*10000100 216*0 8*9 8*0 8*d4 8*0 8*10000100 216*0 8*9 8*0 8*d4 8*0 8*10000100 216*0 8*9 8*0 8*d4
  //   8*0 8*10000100 216*0 8*9 8*0 8*d4 8*0 8*10000100 216*0 8*9 8*0 8*d4 8*0 8*10000100 216*0 8*9 8*0
  //   8*d4 8*0 8*10000100 216*0 8*9 8*0 8*d4 8*0 8*10000100 216*0 8*9 8*0 8*d4 8*0 8*10000100 216*0 8*9
  //   8*0 8*d4 8*0 8*10000100 216*0 8*9 8*0 8*d4 8*0 8*10000100 216*0 8*9 8*0 8*d4 8*0 8*10000100 216*0
  //   8*9 8*0 8*d4 8*0 8*10000100 216*0 8*9 8*0 8*d4 8*0 8*10000100 216*0 8*9 8*0 8*d4 8*0 8*10000100
  //   216*0 8*9 8*0 8*d4 8*0 8*10000100 216*0 8*9 8*0 8*d4 8*0 8*10000100 216*0 8*9 8*0 8*d4 8*0
  //   8*10000100 216*0 8*9 8*0 8*d4 8*0 8*10000100 216*0 8*9 8*0 8*d4 8*0 8*10000100 216*0 8*9 8*0 8*d4
  //   8*0 8*10000100 216*0 8*9 8*0 8*d4 8*0 8*10000100 216*0 8*9 8*0 8*d4 8*0 8*10000100 216*0 8*9 8*0
  //   8*d4 8*0 8*10000100 216*0 8*9 8*0 8*d4 8*0 8*10000100 216*0 8*9 8*0 8*d4 8*0 8*10000100 216*0 8*9
  //   8*0 8*d4 8*0 8*10000100 216*0 8*9 8*0 8*d4 8*0 8*10000100 216*0 8*9 8*0 8*d4 8*0 8*10000100 216*0
  //   8*9 8*0 8*d4 8*0 8*10000100 216*0 8*9 8*0 8*d4 8*0 8*10000100 216*0 8*9 8*0 8*d4 8*0 8*10000100
  //   216*0 8*9 8*0 8*d4 8*0 8*10000100 216*0 8*9 8*0 8*d4 8*0 8*10000100 216*0 8*9 8*0 8*d4 8*0
  //   8*10000100 216*0 8*9 8*0 8*d4 8*0 8*10000100 216*0 8*9 8*0 8*d4 8*0 8*10000100 216*0 8*9 8*0 8*d4
  //   8*0 8*10000100 216*0 8*9 8*0 8*d4 8*0 8*10000100 216*0 8*9 8*0 8*d4 8*0 8*10000100 216*0 8*9 8*0
  //   8*d4 8*0 8*10000100 216*0 8*9 8*0 8*d4 8*0 8*10000100 216*0 8*9 8*0 8*d4 8*0 8*10000100 216*0 8*9
  //   8*0 8*d4 8*0 8*10000100 216*0 8*9 8*0 8*d4 8*0 8*10000100 216*0 8*9 8*0 8*d4 8*0 8*10000100 216*0
  //   8*9 8*0 8*d4 8*0 8*10000100 216*0 8*9 8*0 8*d4 8*0 8*10000100 216*0 8*9 8*0 8*d4 8*0 8*10000100
  //   216*0 8*9 8*0 8*d4 8*0 8*10000100 216*0 8*9 8*0 8*d4 8*0 8*10000100 216*0 8*9 8*0 8*d4 8*0
  //   8*10000100 216*0 8*9 8*0 8*d4 8*0 8*10000100 216*0 8*9 8*0 8*d4 8*0 8*10000100 216*0 8*9 8*0 8*d4
  //   8*0 8*10000100 216*0 8*9 8*0 8*d4 8*0 8*10000100 216*0 8*9 8*0 8*d4 8*0 8*10000100 216*0 8*9 8*0
  //   8*d4 8*0 8*10000100 216*0 8*9 8*0 8*d4 8*0 8*10000100 216*0 8*9 8*0 8*d4 8*0 8*10000100 216*0 8*9
  //   8*0 8*d4 8*0 8*10000100 216*0 8*9 8*0 8*d4 8*0 8*10000100 216*0 8*9 8*0 8*d4 8*0 8*10000100 216*0
  //   8*9 8*0 8*d4 8*0 8*10000100 216*0 8*9 8*0 8*d4 8*0 8*10000100 216*0 8*9 8*0 8*d4 8*0 8*10000100
  //   216*0 8*9 8*0 8*d4 8*0 8*10000100 216*0 8*9 8*0 8*d4 8*0 8*10000100 216*0 8*9 8*0 8*d4 8*0
  //   8*10000100 216*0 8*9 8*0 8*d4 8*0 8*10000100 216*0 8*9 8*0 8*d4 8*0 8*10000100 216*0 8*9 8*0 8*d4
  //   8*0 8*10000100 216*0 8*9 8*0 8*d4 8*0 8*10000100 216*0 8*9 8*0 8*d4 8*0 8*10000100 216*0 8*9 8*0
  //   8*d4 8*0 8*10000100 216*0 8*9 8*0 8*d4 8*0 8*10000100 216*0 8*9 8*0 8*d4 8*0 8*10000100 216*0 8*9
  //   8*0 8*d4 8*0 8*10000100 216*0 8*9 8*0 8*d4 8*0 8*10000100 216*0 8*9 8*0 8*d4 8*0 8*10000100 216*0
  //   8*9 8*0 8*d4 8*0 8*10000100 216*0 8*9 8*0 8*d4 8*0 8*10000100 216*0 8*9 8*0 8*d4 8*0 8*10000100
  //   216*0 8*9 8*0 8*d4 8*0 8*10000100 216*0 8*9 8*0 8*d4 8*0 8*10000100 216*0 8*9 8*0 8*d4 8*0
  //   8*10000100 216*0 8*9 8*0 8*d4 8*0 8*10000100 216*0 8*9 8*0 8*d4 8*0 8*10000100 216*0 8*9 8*0 8*d4
  //   8*0 8*10000100 216*0 8*9 8*0 8*d4 8*0 8*10000100 216*0 8*9 8*0 8*d4 8*0 8*10000100 216*0 8*9 8*0
  //   8*d4 8*0 8*10000100 216*0 8*9 8*0 8*d4 8*0 8*10000100 216*0 8*9 8*0 8*d4 8*0 8*10000100 216*0 8*9
  //   8*0 8*d4 8*0 8*10000100 216*0 8*9 8*0 8*d4 8*0 8*100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
endmodule
